# Fritzing sketch photon-desk-breadboard (saved by Fritzing 0.9.0b)
circuit board: 5.53767cm x 5.58367cm
breadboards: 1

parts:
  R1 = Resistor [tolerance=±5% resistance=220 package=THT]
  IC1 = IC, DIP package, 8 pins [chip_label=LTV-826]
  R2 = Resistor [tolerance=±5% resistance=220 package=THT]
  U1 = RJ45 Jack [package=rj45-8]
  U2 = RJ45 Jack [package=rj45-8]
  Photon = Photon
  J1 = female pin header, 4 pins [form="♀ (female)"]
  Part1 = SRF05 Ultrasonic Rangefinder  # not connected

nets:
  N1: R1.Pin_0, IC1.pin2
  N2: R1.Pin_1, R2.Pin_1, Photon.GND, J1.pin4
  N3: IC1.pin1, Photon.D3
  N4: IC1.pin3, Photon.D4
  N5: IC1.pin4, R2.Pin_0
  N6: IC1.pin5, IC1.pin7, U1.3, U2.3
  N7: IC1.pin8, U1.7, U2.7
  N8: U1.8, U2.8
  N9: Photon.VIN, J1.pin1
  N10: Photon.D5, J1.pin3
  N11: Photon.D6, J1.pin2

notes:
  GeekDeskV3 Controller 1.0
  By TJ Hunter
  github.com/Hypnopompia/photon-desk
